// Logisim project alu.circ as structural Verilog: 1 circuit, main circuit alu
module alu (
  input  [31:0] A,
  input  [31:0] B,
  input  [3:0] ALUSel,
  output [31:0] Result,
  output [31:0] out_5
);

  wire adder_3_cout, aneg, bneg, comparator_1_lt, comparator_3_gt, neg;
  wire [31:0] add, adder_2_out, adder_4_out, adder_5_out, and1, bit_extender_1_out, div1, mul, mulh, mulhu,
       multiplier_1_cout, multiplier_1_out, multiplier_2_cout, newa, newb, or1, rem1, sll1, slt, sra1, srl1,
       sub, xor1, xor_2_out, xor_3_out, xor_5_out;

  Multiplexer #(.select(4), .width(32), .enable("false")) multiplexer_1 (
    .in0(add), .in1(and1), .in2(or1), .in3(xor1), .in4(srl1), .in5(sra1), .in6(sll1), .in7(slt), .in8(div1),
    .in9(rem1), .in10(mul), .in11(mulhu), .in12(sub), .in13(B), .in14(mulh), .out(Result), .sel(ALUSel));  // open: in15
  Shifter #(.width(32), .shift("lr")) shifter_1 (.in(A), .\dist (B[4:0]), .out(srl1));
  Adder #(.width(32)) adder_1 (.a(A), .b(B), .out(add));  // open: cin, cout
  assign and1 = A & B;  // AND_Gate and_1, 32 bits wide
  assign or1 = A | B;  // OR_Gate or_1, 32 bits wide
  assign xor1 = A ^ B;  // XOR_Gate xor_1, 32 bits wide
  Subtractor #(.width(32)) subtractor_1 (.a(A), .b(B), .out(sub));  // open: bin, bout
  Multiplier #(.width(32)) multiplier_1 (
    .a(newb), .b(newa), .out(multiplier_1_out), .cout(multiplier_1_cout));  // open: cin
  assign xor_2_out = multiplier_1_out ^ {32{1'b1}};  // XOR_Gate xor_2, 32 bits wide
  assign xor_3_out = multiplier_1_cout ^ {32{1'b1}};  // XOR_Gate xor_3, 32 bits wide
  assign out_5 = B ^ {32{1'b1}};  // XOR_Gate xor_4, 32 bits wide
  Adder #(.width(32)) adder_2 (.a(out_5), .b(32'h1), .out(adder_2_out));  // open: cin, cout
  Adder #(.width(32)) adder_3 (.a(xor_2_out), .b(32'h1), .cout(adder_3_cout));  // open: out, cin
  assign bit_extender_1_out = {{31{1'b0}}, adder_3_cout};  // Bit_Extender bit_extender_1
  Shifter #(.width(32), .shift("ar")) shifter_2 (.in(A), .\dist (B[4:0]), .out(sra1));
  Shifter #(.width(32)) shifter_3 (.in(A), .\dist (B[4:0]), .out(sll1));
  Divider #(.width(32)) divider_1 (.a(A), .b(B), .out(div1));  // open: upper, rem
  Divider #(.width(32)) divider_2 (.a(A), .b(B), .rem(rem1));  // open: out, upper
  Multiplexer #(.width(32), .enable("false")) multiplexer_2 (.in0(B), .in1(adder_2_out), .out(newb), .sel(bneg));
  Adder #(.width(32)) adder_4 (.a(bit_extender_1_out), .b(xor_3_out), .out(adder_4_out));  // open: cin, cout
  Comparator #(.width(32)) comparator_1 (.a(A), .b(B), .lt(comparator_1_lt));  // open: gt, eq
  assign slt = {{31{1'b0}}, comparator_1_lt};  // Bit_Extender bit_extender_2
  Multiplier #(.width(32)) multiplier_2 (.a(newb), .b(newa), .cout(multiplier_2_cout));  // open: out, cin
  Multiplier #(.width(32)) multiplier_3 (.a(A), .b(B), .out(mul));  // open: cin, cout
  Multiplier #(.width(32)) multiplier_4 (.a(A), .b(B), .cout(mulhu));  // open: out, cin
  assign xor_5_out = A ^ {32{1'b1}};  // XOR_Gate xor_5, 32 bits wide
  Comparator #(.width(32)) comparator_2 (.a(A), .b({32{1'b0}}), .lt(aneg));  // open: gt, eq
  Comparator #(.width(32)) comparator_3 (.a(B), .b({32{1'b0}}), .gt(comparator_3_gt), .lt(bneg));  // open: eq
  Multiplexer #(.width(32), .enable("false")) multiplexer_3 (.in0(A), .in1(adder_5_out), .out(newa), .sel(aneg));
  Adder #(.width(32)) adder_5 (.a(xor_5_out), .b(32'h1), .out(adder_5_out));  // open: cin, cout
  Multiplexer #(.width(32), .enable("false")) multiplexer_4 (
    .in0(multiplier_2_cout), .in1(adder_4_out), .out(mulh), .sel(neg));
  xor xor_6 (neg, aneg, bneg);

  // Other names for the same wires on the sheet: bsel[31:0] = B

  // Notes on the sheet:
  //   INPUTS to your circuit
  //   DON'T CHANGE THE LOCATIONS OF THE INPUTS AND OUTPUTS!
  //   OUTPUT from your circuit
endmodule
