// Logisim project cpu.circ as structural Verilog: 9 circuits, main circuit main
module main (
  input  [31:0] INSTRUCTION,
  input  CLOCK,
  output [31:0] FETCH_ADDRESS,
  output [31:0] ra,
  output [31:0] sp,
  output [31:0] t0,
  output [31:0] t1,
  output [31:0] t2,
  output [31:0] s0,
  output [31:0] s1,
  output [31:0] a0
);

  wire ASel, B, BrEq, BrLt, BrNe, BrUn, BSel, DMEM_p1, DMEM_p2, DMEM_p8, DMEM_p10, I, J, MemRW, PCSel, R,
       REGWen, S, U;
  wire [1:0] WBSel;
  wire [2:0] bitfinder_1_index, ImmSel;
  wire [3:0] ALUSel;
  wire [5:1] comparator_1_eq;
  wire [31:0] adder_1_out, alu_1_result, Bimm, DMEM_p11, Iimm, Immediate, Jimm, multiplexer_1_out,
       multiplexer_2_out, multiplexer_3_out, multiplexer_4_out, multiplexer_5_out, oldINSTRUCTION, PC2_q,
       PCminus4_q, PROGRAM_COUNTER, r1, r2, Simm, Uimm;

  Shifter #(.width(32), .shift("lr")) shifter_1 (.in(PROGRAM_COUNTER), .\dist (5'b00010), .out(FETCH_ADDRESS));
  Adder #(.width(32)) adder_1 (.a(PROGRAM_COUNTER), .b(32'h4), .out(adder_1_out));  // open: cin, cout
  Multiplexer #(.width(32), .enable("false")) multiplexer_1 (
    .in0(adder_1_out), .in1(alu_1_result), .out(multiplexer_1_out), .sel(PCSel));
  Register #(.width(32)) PC2 (.D(adder_1_out), .clk(CLOCK), .Q(PC2_q));  // open: en, clr
  Register #(.width(32)) PC (.D(multiplexer_1_out), .clk(CLOCK), .Q(PROGRAM_COUNTER));  // open: en, clr
  Register #(.width(32)) storeinstruc (.D(multiplexer_2_out), .clk(CLOCK), .Q(oldINSTRUCTION));  // open: en, clr
  Multiplexer #(.width(32), .enable("false")) multiplexer_2 (
    .in0(INSTRUCTION), .in1(32'h13), .out(multiplexer_2_out), .sel(PCSel));
  Register #(.width(32)) PCminus4 (.D(PROGRAM_COUNTER), .clk(CLOCK), .Q(PCminus4_q));  // open: en, clr
  controlMod controlmod_1 (
    .instruction(oldINSTRUCTION), .r2(r2), .r1(r1), .out_4(BrNe), .BrEq(BrEq), .BrLt(BrLt), .PCSel(PCSel),
    .ImmSel(ImmSel), .BrUn(BrUn), .ASel(ASel), .BSel(BSel), .ALUSel(ALUSel), .MemRW(MemRW), .REGWen(REGWen),
    .WBSel(WBSel), .Itype(I), .Stype(S), .Btype(B), .Utype(U), .Jtype(J), .R(R));
  // Probe on r1
  regfile_main RegFile (
    .rs2(oldINSTRUCTION[24:20]), .rd(oldINSTRUCTION[11:7]), .Read_Data_1(r1), .Read_Data_2(r2), .ra(ra),
    .sp(sp), .t0(t0), .t1(t1), .t2(t2), .s0(s0), .s1(s1), .a0(a0), .rs1(oldINSTRUCTION[19:15]),
    .Write_Data(multiplexer_5_out), .RegWEn(REGWen), .clk(CLOCK));
  // Probe on r2
  // Probe on multiplexer_3_out
  Multiplexer #(.width(32), .enable("false")) multiplexer_3 (
    .in0(PCminus4_q), .in1(r1), .out(multiplexer_3_out), .sel(ASel));
  // Probe on multiplexer_4_out
  Multiplexer #(.width(32), .enable("false")) multiplexer_4 (
    .in0(r2), .in1(Immediate), .out(multiplexer_4_out), .sel(BSel));
  alu alu_1 (.A(multiplexer_3_out), .B(multiplexer_4_out), .ALUSel(ALUSel), .Result(alu_1_result));
  Comparator #(.width(1)) comparator_1 (.a(I), .b(1'b1), .eq(comparator_1_eq[1]));  // open: gt, lt
  Comparator #(.width(1)) comparator_2 (.a(S), .b(1'b1), .eq(comparator_1_eq[2]));  // open: gt, lt
  Comparator #(.width(1)) comparator_3 (.a(B), .b(1'b1), .eq(comparator_1_eq[3]));  // open: gt, lt
  // Probe on alu_1_result
  Comparator #(.width(1)) comparator_4 (.a(U), .b(1'b1), .eq(comparator_1_eq[4]));  // open: gt, lt
  Comparator #(.width(1)) comparator_5 (.a(J), .b(1'b1), .eq(comparator_1_eq[5]));  // open: gt, lt
  Btypecircuit btypecircuit_1 (.in_1(oldINSTRUCTION), .immediate(Bimm));  // open: func3, rs1, rs2, Opcode
  Itypecircuit itypecircuit_1 (
    .in_1(oldINSTRUCTION), .Immediate(Iimm));  // open: Opcode, out_3, out_4, out_5, out_6, out_7
  // Probe on DMEM_p11
  // mem_main DMEM: pin names not known; wires that end beside it: DMEM_p1, DMEM_p2, alu_1_result, r2, MemRW, CLOCK, DMEM_p2, DMEM_p8, DMEM_p8, DMEM_p10, DMEM_p11
  BitFinder #(.width(6)) bitfinder_1 (.in({comparator_1_eq, R}), .index(bitfinder_1_index));  // open: found
  Multiplexer #(.select(2), .width(32), .enable("false")) multiplexer_5 (
    .in0(DMEM_p11), .in1(alu_1_result), .in2(PC2_q), .out(multiplexer_5_out), .sel(WBSel));  // open: in3
  Multiplexer #(.select(3), .width(32), .enable("false")) multiplexer_6 (
    .in1(Iimm), .in2(Simm), .in3(Bimm), .in4(Uimm), .in5(Jimm), .out(Immediate), .sel(bitfinder_1_index));  // open: in0, in6, in7
  Stypecircuit stypecircuit_1 (.in_1(oldINSTRUCTION), .Immediate(Simm));  // open: out_2, out_3, out_4, out_5
  Utypecircuit utypecircuit_1 (.in_1(oldINSTRUCTION), .immediate(Uimm));  // open: out_2, out_3
  Jtypecircuit jtypecircuit_1 (.in_1(oldINSTRUCTION), .immediate(Jimm));  // open: out_2, out_3

  // Other names for the same wires on the sheet: clk = CLOCK

  // Notes on the sheet:
  //   Output
  //   Inputs/Outputs from run.circ. DO NOT MOVE THESE.
  //   Inputs
  //   It is OK to move the PC, RegFile, ALU, and MEM to wherever is most convenient for you when constructing your CPU, and to delete this text
  //   Inputs/Outputs from run.circ. DO NOT MOVE THESE.
endmodule

module ImmGenerator (
  input  [11:0] in_1,
  output [31:0] out_2
);

  assign out_2 = {{20{1'b0}}, in_1};  // Bit_Extender bit_extender_1
endmodule

module controlMod (
  input  [31:0] instruction,
  input  [31:0] r2,
  input  [31:0] r1,
  output out_4,
  output BrEq,
  output BrLt,
  output PCSel,
  output [2:0] ImmSel,
  output BrUn,
  output ASel,
  output BSel,
  output [3:0] ALUSel,
  output MemRW,
  output REGWen,
  output [1:0] WBSel,
  output Itype,
  output Stype,
  output Btype,
  output Utype,
  output Jtype,
  output R
);

  wire and_1_out, and_2_out, and_3_out, and_4_out, and_5_out, and_6_out, and_7_out, and_8_out,
       bitfinder_2_index, bitfinder_3_index, bitfinder_4_index, bitfinder_5_index, bitfinder_8_index,
       comparator_61_eq, comparator_62_eq, comparator_70_eq, comparator_72_eq, comparator_75_eq,
       comparator_76_eq, Equal, initialInstruc, isadd, isaddi, isand1, isandi, isbeq, isblt, isbltu, isbne,
       isdivu, isjal, isjalr, islb, islh, islui, islw, islwc, ismul, ismulh, ismulhu, isor1, isori, ispop,
       ispush, isremu, issll1, isslli, isslt, isslti, issra1, issrai, issrl1, issrli, issub, issw, isxor1,
       isxori, Itype_t, lessornot, lessornotunsigned, Lessthan, not_1_out, not_2_out, not_3_out, NotEqual,
       or_1_out, or_2_out, or_3_out, or_4_out, or_5_out, or_6_out, or_7_out, or_8_out, or_9_out, or_10_out,
       or_11_out, or_12_out, or_13_out, or_14_out, or_15_out, or_16_out, or_17_out, or_18_out, or_21_out,
       or_22_out, or_23_out, or_24_out, PrePCSel;
  wire [1:0] bitfinder_1_index, comparator_9_eq, comparator_13_eq, comparator_22_eq, comparator_34_eq,
       comparator_74_eq;
  wire [2:0] bitfinder_7_index, comparator_10_eq, func3;
  wire [3:0] bitfinder_6_index;
  wire [4:0] comparator_46_eq, rs1, rs2;
  wire [6:0] func7, instruc;
  wire [7:0] comparator_48_eq;

  Rtype rtype_1 (.in_1(instruction), .func3(func3), .rs1(rs1), .rs2(rs2), .Opcode(instruc), .func7(func7));  // open: Rd
  Comparator #(.width(17)) comparator_1 (.a({func7, func3, instruc}), .b(17'h33), .eq(isadd));  // open: gt, lt
  Comparator #(.width(17)) comparator_2 (.a({func7, func3, instruc}), .b(17'h5b3), .eq(ismulhu));  // open: gt, lt
  Comparator #(.width(17)) comparator_3 (.a({func7, func3, instruc}), .b(17'h2b3), .eq(issrl1));  // open: gt, lt
  Comparator #(.width(17)) comparator_4 (.a({func7, func3, instruc}), .b(17'h7b3), .eq(isremu));  // open: gt, lt
  Comparator #(.width(10)) comparator_5 (.a({func3, instruc}), .b(10'h103), .eq(islw));  // open: gt, lt
  Comparator #(.width(10)) comparator_6 (.a({func3, instruc}), .b(10'he3), .eq(isbne));  // open: gt, lt
  Comparator #(.width(1)) comparator_7 (.a(issw), .b(1'b1), .eq(MemRW));  // open: gt, lt
  or or_1 (or_1_out, isblt, isslti, isslt);
  or or_2 (or_2_out, islb, islw, islh);
  or or_3 (or_3_out, isjalr, isjal);
  or or_4 (or_4_out, isjalr, Btype, Itype_t, Utype, Stype, Jtype);
  or or_5 (or_5_out, R, Itype_t, Stype, isjalr);
  Comparator #(.width(10)) comparator_8 (.a({func3, instruc}), .b(10'h123), .eq(issw));  // open: gt, lt
  Comparator #(.width(1)) comparator_9 (.a(or_1_out), .b(1'b1), .eq(comparator_9_eq[0]));  // open: gt, lt
  Comparator #(.width(1)) comparator_10 (.a(or_2_out), .b(1'b1), .eq(comparator_10_eq[0]));  // open: gt, lt
  or or_6 (or_6_out, islui, R, isaddi, isslli, isslti, issrli, issrai, isori, isandi, isxori);
  Comparator #(.width(1)) comparator_11 (.a(or_6_out), .b(1'b1), .eq(comparator_10_eq[1]));  // open: gt, lt
  Comparator #(.width(1)) comparator_12 (.a(or_3_out), .b(1'b1), .eq(comparator_10_eq[2]));  // open: gt, lt
  Comparator #(.width(1)) comparator_13 (.a(R), .b(1'b1), .eq(comparator_13_eq[0]));  // open: gt, lt
  Comparator #(.width(1)) comparator_14 (.a(or_4_out), .b(1'b1), .eq(comparator_13_eq[1]));  // open: gt, lt
  or or_7 (or_7_out, Btype, Utype, Jtype);
  Comparator #(.width(1)) comparator_15 (.a(or_5_out), .b(1'b1), .eq(comparator_22_eq[1]));  // open: gt, lt
  Comparator #(.width(17)) comparator_16 (.a({func7, func3, instruc}), .b(17'h233), .eq(isxor1));  // open: gt, lt
  Comparator #(.width(17)) comparator_17 (.a({func7, func3, instruc}), .b(17'h82b3), .eq(issra1));  // open: gt, lt
  Comparator #(.width(17)) comparator_18 (.a({func7, func3, instruc}), .b(17'h3b3), .eq(isand1));  // open: gt, lt
  Comparator #(.width(10)) comparator_19 (.a({func3, instruc}), .b(10'h13), .eq(isaddi));  // open: gt, lt
  Comparator #(.width(10)) comparator_20 (.a({func3, instruc}), .b(10'h293), .eq(issrli));  // open: gt, lt
  Comparator #(.width(1)) comparator_21 (.a(isbltu), .b(1'b1), .eq(comparator_9_eq[1]));  // open: gt, lt
  Comparator #(.width(1)) comparator_22 (.a(or_7_out), .b(1'b1), .eq(comparator_22_eq[0]));  // open: gt, lt
  BitFinder #(.width(3)) bitfinder_1 (.in(comparator_10_eq), .index(bitfinder_1_index));  // open: found
  Multiplexer #(.enable("false")) multiplexer_1 (.in0(1'b0), .in1(1'b1), .out(BSel), .sel(bitfinder_2_index));
  BitFinder #(.width(2)) bitfinder_2 (.in(comparator_13_eq), .index(bitfinder_2_index));  // open: found
  Comparator #(.width(7)) comparator_23 (.a(instruc), .b(7'b0110111), .eq(islui));  // open: gt, lt
  Comparator #(.width(10)) comparator_24 (.a({func3, instruc}), .b(10'h63), .eq(isbeq));  // open: gt, lt
  Comparator #(.width(17)) comparator_25 (.a({func7, func3, instruc}), .b(17'h333), .eq(isor1));  // open: gt, lt
  Comparator #(.width(10)) comparator_26 (.a({func3, instruc}), .b(10'h3), .eq(islb));  // open: gt, lt
  Comparator #(.width(17)) comparator_27 (.a({func7, func3, instruc}), .b(17'h93), .eq(isslli));  // open: gt, lt
  Comparator #(.width(17)) comparator_28 (.a({func7, func3, instruc}), .b(17'h8293), .eq(issrai));  // open: gt, lt
  BitFinder #(.width(2)) bitfinder_3 (.in(comparator_9_eq), .index(bitfinder_3_index));  // open: found
  Multiplexer #(.select(2), .width(2), .enable("false")) multiplexer_2 (
    .in0(2'b00), .in1(2'b01), .in2(2'b10), .out(WBSel), .sel(bitfinder_1_index));  // open: in3
  Multiplexer #(.enable("false")) multiplexer_3 (.in0(1'b0), .in1(1'b1), .out(ASel), .sel(bitfinder_4_index));
  BitFinder #(.width(2)) bitfinder_4 (.in(comparator_22_eq), .index(bitfinder_4_index));  // open: found
  Comparator #(.width(17)) comparator_29 (.a({func7, func3, instruc}), .b(17'h33), .eq(isadd));  // open: gt, lt
  Multiplexer #(.enable("false")) multiplexer_4 (.in0(1'b0), .in1(1'b1), .out(BrUn), .sel(bitfinder_3_index));
  or or_8 (or_8_out, Jtype, Itype_t, isjalr, R, Utype);
  or or_9 (or_9_out, isadd, islw, issw, isjal, islb, Btype, isjalr, isaddi, islh);
  or or_10 (or_10_out, isand1, isandi);
  or or_11 (or_11_out, isor1, isori);
  or or_12 (or_12_out, isxori, isxor1);
  or or_13 (or_13_out, issrl1, issrli);
  or or_14 (or_14_out, issra1, issrai);
  or or_15 (or_15_out, issll1, isslli);
  or or_16 (or_16_out, isslt, isslti);
  Comparator #(.width(17)) comparator_30 (.a({func7, func3, instruc}), .b(17'h8033), .eq(issub));  // open: gt, lt
  Comparator #(.width(17)) comparator_31 (.a({func7, func3, instruc}), .b(17'h433), .eq(ismul));  // open: gt, lt
  Comparator #(.width(10)) comparator_32 (.a({func3, instruc}), .b(10'h83), .eq(islh));  // open: gt, lt
  Comparator #(.width(17)) comparator_33 (.a({func7, func3, instruc}), .b(17'h113), .eq(isslti));  // open: gt, lt
  or or_17 (or_17_out, Stype, Btype);
  Comparator #(.width(1)) comparator_34 (.a(or_17_out), .b(1'b1), .eq(comparator_34_eq[0]));  // open: gt, lt
  Comparator #(.width(1)) comparator_35 (.a(or_8_out), .b(1'b1), .eq(comparator_34_eq[1]));  // open: gt, lt
  Comparator #(.width(1)) comparator_36 (.a(or_10_out), .b(1'b1), .eq(comparator_48_eq[1]));  // open: gt, lt
  Comparator #(.width(1)) comparator_37 (.a(or_11_out), .b(1'b1), .eq(comparator_48_eq[2]));  // open: gt, lt
  Comparator #(.width(1)) comparator_38 (.a(or_12_out), .b(1'b1), .eq(comparator_48_eq[3]));  // open: gt, lt
  Comparator #(.width(1)) comparator_39 (.a(or_13_out), .b(1'b1), .eq(comparator_48_eq[4]));  // open: gt, lt
  Comparator #(.width(1)) comparator_40 (.a(or_14_out), .b(1'b1), .eq(comparator_48_eq[5]));  // open: gt, lt
  Comparator #(.width(1)) comparator_41 (.a(or_15_out), .b(1'b1), .eq(comparator_48_eq[6]));  // open: gt, lt
  Comparator #(.width(1)) comparator_42 (.a(or_16_out), .b(1'b1), .eq(comparator_48_eq[7]));  // open: gt, lt
  Comparator #(.width(7)) comparator_43 (.a(instruc), .b(7'b1101111), .eq(isjal));  // open: gt, lt
  Comparator #(.width(10)) comparator_44 (.a({func3, instruc}), .b(10'h263), .eq(isblt));  // open: gt, lt
  Comparator #(.width(10)) comparator_45 (.a({func3, instruc}), .b(10'h313), .eq(isori));  // open: gt, lt
  Comparator #(.width(1)) comparator_46 (.a(Itype_t), .b(1'b1), .eq(comparator_46_eq[0]));  // open: gt, lt
  Comparator #(.width(1)) comparator_47 (.a(Stype), .b(1'b1), .eq(comparator_46_eq[1]));  // open: gt, lt
  Comparator #(.width(1)) comparator_48 (.a(or_9_out), .b(1'b1), .eq(comparator_48_eq[0]));  // open: gt, lt
  Comparator #(.width(17)) comparator_49 (.a({func7, func3, instruc}), .b(17'h133), .eq(isslt));  // open: gt, lt
  Comparator #(.width(17)) comparator_50 (.a({func7, func3, instruc}), .b(17'h4b3), .eq(ismulh));  // open: gt, lt
  Comparator #(.width(17)) comparator_51 (.a({func7, func3, instruc}), .b(17'hb3), .eq(issll1));  // open: gt, lt
  Comparator #(.width(1)) comparator_52 (.a(Btype), .b(1'b1), .eq(comparator_46_eq[2]));  // open: gt, lt
  BitFinder #(.width(2)) bitfinder_5 (.in(comparator_34_eq), .index(bitfinder_5_index));  // open: found
  Comparator #(.width(7)) comparator_53 (.a(instruc), .b(7'b0110011), .eq(R));  // open: gt, lt
  Comparator #(.width(17)) comparator_54 (.a({func7, func3, instruc}), .b(17'h6b3), .eq(isdivu));  // open: gt, lt
  Comparator #(.width(10)) comparator_55 (.a({func3, instruc}), .b(10'h67), .eq(isjalr));  // open: gt, lt
  Comparator #(.width(10)) comparator_56 (.a({func3, instruc}), .b(10'h363), .eq(isbltu));  // open: gt, lt
  Comparator #(.width(10)) comparator_57 (.a({func3, instruc}), .b(10'h213), .eq(isxori));  // open: gt, lt
  Comparator #(.width(10)) comparator_58 (.a({func3, instruc}), .b(10'h393), .eq(isandi));  // open: gt, lt
  Comparator #(.width(1)) comparator_59 (.a(Utype), .b(1'b1), .eq(comparator_46_eq[3]));  // open: gt, lt
  Multiplexer #(.enable("false")) multiplexer_5 (.in0(1'b0), .in1(1'b1), .out(REGWen), .sel(bitfinder_5_index));
  BitFinder #(.width(15)) bitfinder_6 (
    .in({ismulh, islui, issub, ismulhu, ismul, isremu, isdivu, comparator_48_eq}), .index(bitfinder_6_index));  // open: found
  Multiplexer #(.select(4), .width(4), .enable("false")) multiplexer_6 (
    .in0(4'b0000), .in1(4'b0001), .in2(4'b0010), .in3(4'b0011), .in4(4'b0100), .in5(4'b0101), .in6(4'b0110),
    .in7(4'b0111), .in8(4'b1000), .in9(4'b1001), .in10(4'b1010), .in11(4'b1011), .in12(4'b1100),
    .in13(4'b1101), .in14(4'b1110), .in15(4'b1111), .out(ALUSel), .sel(bitfinder_6_index));
  Comparator #(.width(1)) comparator_60 (.a(Jtype), .b(1'b1), .eq(comparator_46_eq[4]));  // open: gt, lt
  not not_1 (not_1_out, lessornotunsigned);
  not not_2 (not_2_out, lessornot);
  Comparator #(.width(7)) comparator_61 (.a(instruc), .b(7'b0010011), .eq(comparator_61_eq));  // open: gt, lt
  or or_18 (or_18_out, comparator_61_eq, comparator_62_eq);
  Comparator #(.width(7)) comparator_62 (.a(instruc), .b(7'b0000011), .eq(comparator_62_eq));  // open: gt, lt
  Comparator #(.width(7)) comparator_63 (.a(instruc), .b(7'b0100011), .eq(Stype));  // open: gt, lt
  Comparator #(.width(7)) comparator_64 (.a(instruc), .b(7'b1100011), .eq(Btype));  // open: gt, lt
  Comparator #(.width(7)) comparator_65 (.a(instruc), .b(7'b0110111), .eq(Utype));  // open: gt, lt
  Comparator #(.width(7)) comparator_66 (.a(instruc), .b(7'b1101111), .eq(Jtype));  // open: gt, lt
  Comparator #(.width(10)) comparator_67 (.a({func3, instruc}), .b(10'h383), .eq(islwc));  // open: gt, lt
  Comparator #(.width(10)) comparator_68 (.a({func3, instruc}), .b(10'h1bb), .eq(ispush));  // open: gt, lt
  Comparator #(.width(10)) comparator_69 (.a({func3, instruc}), .b(10'h13b), .eq(ispop));  // open: gt, lt
  and and_1 (and_1_out, not_1_out, isbltu);
  and and_2 (and_2_out, not_2_out, isblt);
  and and_3 (and_3_out, NotEqual, isbeq);
  and and_4 (and_4_out, Equal, isbne);
  buf or_19 (Itype_t, or_18_out);  // OR_Gate
  Multiplexer #(.select(3), .width(3), .enable("false")) multiplexer_7 (
    .in0(3'b000), .in1(3'b001), .in2(3'b010), .in3(3'b011), .in4(3'b100), .out(ImmSel),
    .sel(bitfinder_7_index));  // open: in5, in6, in7
  BitFinder #(.width(5)) bitfinder_7 (.in(comparator_46_eq), .index(bitfinder_7_index));  // open: found
  not not_3 (not_3_out, Equal);
  Comparator #(.width(7)) comparator_70 (.a(instruc), .b(7'b1100111), .eq(comparator_70_eq));  // open: gt, lt
  or or_20 (Itype, comparator_70_eq, Itype_t);
  Comparator #(.width(32), .mode("unsigned")) comparator_71 (
    .a(r1), .b(r2), .eq(Equal), .lt(lessornotunsigned));  // open: gt
  Comparator #(.width(32)) comparator_72 (.a(instruction), .b({32{1'b0}}), .eq(comparator_72_eq));  // open: gt, lt
  or or_21 (or_21_out, and_1_out, and_2_out, and_3_out, and_4_out, R, Itype_t, Stype, Utype);
  or or_22 (or_22_out, Jtype, isjalr);
  and and_5 (and_5_out, Equal, isbeq);
  and and_6 (and_6_out, lessornotunsigned, isbltu);
  and and_7 (and_7_out, lessornot, isblt);
  and and_8 (and_8_out, not_3_out, isbne);
  Comparator #(.width(32)) comparator_73 (.a(r1), .b(r2), .lt(lessornot));  // open: gt, eq
  and and_9 (out_4, isbne, NotEqual);
  not not_4 (initialInstruc, comparator_72_eq);
  Comparator #(.width(1)) comparator_74 (.a(or_21_out), .b(1'b1), .eq(comparator_74_eq[0]));  // open: gt, lt
  Comparator #(.width(1)) comparator_75 (.a(or_22_out), .b(1'b1), .eq(comparator_75_eq));  // open: gt, lt
  or or_23 (or_23_out, and_5_out, and_6_out, and_7_out, and_8_out);
  or or_24 (or_24_out, isblt, isbltu);
  or or_25 (comparator_74_eq[1], comparator_75_eq, comparator_76_eq);
  Comparator #(.width(1)) comparator_76 (.a(or_23_out), .b(1'b1), .eq(comparator_76_eq));  // open: gt, lt
  not not_5 (NotEqual, Equal);
  Multiplexer #(.enable("false")) multiplexer_8 (.in0(lessornot), .in1(lessornotunsigned), .out(Lessthan), .sel(BrUn));
  and and_10 (PCSel, PrePCSel, initialInstruc);
  Multiplexer #(.enable("false")) multiplexer_9 (.in0(1'b0), .in1(1'b1), .out(PrePCSel), .sel(bitfinder_8_index));
  BitFinder #(.width(2)) bitfinder_8 (.in(comparator_74_eq), .index(bitfinder_8_index));  // open: found
  and and_11 (BrLt, or_24_out, Lessthan);
  and and_12 (BrEq, isbeq, Equal);

  // Other names for the same wires on the sheet: BrNe = out_4; no7instruc[9:0] = {func3, instruc};
  //   Opcode[6:0] = instruc; instruc[16:7] = {func7, func3}; Itypefinal = Itype; Rtype = R
endmodule

module Rtype (
  input  [31:0] in_1,
  output [4:0] Rd,
  output [2:0] func3,
  output [4:0] rs1,
  output [4:0] rs2,
  output [6:0] Opcode,
  output [6:0] func7
);


  assign func3 = in_1[14:12];
  assign func7 = in_1[31:25];
  assign Opcode = in_1[6:0];
  assign Rd = in_1[11:7];
  assign rs1 = in_1[19:15];
  assign rs2 = in_1[24:20];
endmodule

module Itypecircuit (
  input  [31:0] in_1,
  output [6:0] Opcode,
  output [4:0] out_3,
  output [2:0] out_4,
  output [2:0] out_5,
  output [4:0] out_6,
  output [4:0] out_7,
  output [31:0] Immediate
);

  assign Immediate = {{20{in_1[31]}}, in_1[31:20]};  // Bit_Extender bit_extender_1

  assign Opcode = in_1[6:0];
  assign out_3 = in_1[11:7];
  assign out_4 = in_1[14:12];
  assign out_5 = in_1[14:12];
  assign out_6 = in_1[19:15];
  assign out_7 = in_1[19:15];

  // Other names for the same wires on the sheet: rd[4:0] = in_1[11:7]; func3[2:0] = in_1[14:12];
  //   rs1[4:0] = in_1[19:15]; preImmediate[11:0] = in_1[31:20]
endmodule

module Stypecircuit (
  input  [31:0] in_1,
  output [4:0] out_2,
  output [4:0] out_3,
  output [6:0] out_4,
  output [2:0] out_5,
  output [31:0] Immediate
);

  assign Immediate = {{20{in_1[31]}}, {in_1[31:25], in_1[11:7]}};  // Bit_Extender bit_extender_1

  assign out_2 = in_1[19:15];
  assign out_3 = in_1[24:20];
  assign out_4 = in_1[6:0];
  assign out_5 = in_1[14:12];

  // Other names for the same wires on the sheet: imm1[4:0] = in_1[11:7]; imm2[6:0] = in_1[31:25];
  //   Opcode[6:0] = in_1[6:0]; func3[2:0] = in_1[14:12]; rs1[4:0] = in_1[19:15]; rs2[4:0] = in_1[24:20]
endmodule

module Btypecircuit (
  input  [31:0] in_1,
  output [2:0] func3,
  output [4:0] rs1,
  output [4:0] rs2,
  output [6:0] Opcode,
  output [31:0] immediate
);

  assign immediate = {{19{in_1[31]}}, {in_1[31], in_1[7], in_1[30:25], in_1[11:8], 1'b0}};  // Bit_Extender bit_extender_1

  assign func3 = in_1[14:12];
  assign Opcode = in_1[6:0];
  assign rs1 = in_1[19:15];
  assign rs2 = in_1[24:20];

  // Other names for the same wires on the sheet: imm1[4:0] = in_1[11:7];
  //   immediateoops[11:0] = {in_1[31], in_1[7], in_1[30:25], in_1[11:8]}; imm2[6:0] = in_1[31:25]
endmodule

module Utypecircuit (
  input  [31:0] in_1,
  output [6:0] out_2,
  output [4:0] out_3,
  output [31:0] immediate
);


  assign immediate = {in_1[31:12], {12{1'b0}}};
  assign out_2 = in_1[6:0];
  assign out_3 = in_1[11:7];

  // Other names for the same wires on the sheet: preImmediate[19:0] = in_1[31:12]; Opcode[6:0] = in_1[6:0];
  //   rd[4:0] = in_1[11:7]
endmodule

module Jtypecircuit (
  input  [31:0] in_1,
  output [6:0] out_2,
  output [4:0] out_3,
  output [31:0] immediate
);

  assign immediate = {{11{in_1[31]}}, {in_1[31], in_1[19:12], in_1[20], in_1[30:21], 1'b0}};  // Bit_Extender bit_extender_1

  assign out_2 = in_1[6:0];
  assign out_3 = in_1[11:7];

  // Other names for the same wires on the sheet: preImmediate[19:0] = in_1[31:12]; Opcode[6:0] = in_1[6:0];
  //   rd[4:0] = in_1[11:7]
endmodule
